// Logisim project RusLucianFlorin_CircuitCombinational.circ as structural Verilog: 1 circuit, main circuit main
module main (
  input  x,
  input  y,
  input  z,
  output A,
  output B,
  output C
);

  RusLucianFlorin_CircuitSumator_main main (.ai(x), .bi(y), .Ti_1(z), .Si(A), .Ti(B));
  not not_1 (C, y);
endmodule
