// Logisim project RusLucianFlorin_CircuitDecodor.circ as structural Verilog: 1 circuit, main circuit main
module main (
  input  a,
  input  b,
  input  c,
  output a_prime_b_prime_c_prime,
  output a_prime_b_prime_c,
  output a_prime_bc_prime,
  output a_prime_bc,
  output ab_prime_c_prime,
  output ab_prime_c,
  output abc_prime,
  output abc
);

  wire not_1_out;

  Decoder #(.select(2)) decoder_1 (
    .out0(a_prime_b_prime_c_prime), .out1(a_prime_b_prime_c), .out2(a_prime_bc_prime), .out3(a_prime_bc),
    .sel({b, c}), .en(not_1_out));
  not not_1 (not_1_out, a);
  Decoder #(.select(2)) decoder_2 (
    .out0(ab_prime_c_prime), .out1(ab_prime_c), .out2(abc_prime), .out3(abc), .sel({b, c}), .en(a));
endmodule
