// Logisim project RusLucianFlorin_CircuitRegistruDeplasare.circ as structural Verilog: 1 circuit, main circuit main
module main (
  input  Serial_Input,
  input  I0,
  input  I1,
  input  I2,
  input  Serial_Input_2,
  input  I3,
  input  S0,
  input  S1,
  output A0,
  output A1,
  output A2,
  output A3
);

  wire Clock_out, multiplexer_1_out, multiplexer_2_out, multiplexer_3_out, multiplexer_4_out;

  Clock Clock (.out(Clock_out));
  Multiplexer #(.select(2), .enable("false")) multiplexer_1 (
    .in0(A0), .in1(Serial_Input), .in2(A1), .in3(I0), .out(multiplexer_1_out), .sel({S1, S0}));
  Multiplexer #(.select(2), .enable("false")) multiplexer_2 (
    .in0(A1), .in1(A0), .in2(A2), .in3(I1), .out(multiplexer_2_out), .sel({S1, S0}));
  Multiplexer #(.select(2), .enable("false")) multiplexer_3 (
    .in0(A2), .in1(A1), .in2(A3), .in3(I2), .out(multiplexer_3_out), .sel({S1, S0}));
  Multiplexer #(.select(2), .enable("false")) multiplexer_4 (
    .in0(A3), .in1(A2), .in2(Serial_Input_2), .in3(I3), .out(multiplexer_4_out), .sel({S1, S0}));
  D_Flip_Flop d_ff_1 (.clk(Clock_out), .D(multiplexer_1_out), .Q(A0));  // open: Qn, preset, en, reset
  D_Flip_Flop d_ff_2 (.clk(Clock_out), .D(multiplexer_2_out), .Q(A1));  // open: Qn, preset, en, reset
  D_Flip_Flop d_ff_3 (.clk(Clock_out), .D(multiplexer_3_out), .Q(A2));  // open: Qn, preset, en, reset
  D_Flip_Flop d_ff_4 (.clk(Clock_out), .D(multiplexer_4_out), .Q(A3));  // open: Qn, preset, en, reset
endmodule
