// Logisim project RusLucianFlorin_CircuitSumator.circ as structural Verilog: 1 circuit, main circuit main
module main (
  input  ai,
  input  bi,
  input  Ti_1,
  output Si,
  output Ti
);

  wire and_1_out, and_2_out, xor_1_out;

  xor xor_1 (xor_1_out, ai, bi);
  and and_1 (and_1_out, bi, ai);
  and and_2 (and_2_out, xor_1_out, Ti_1);
  xor xor_2 (Si, xor_1_out, Ti_1);
  or or_1 (Ti, and_2_out, and_1_out);

  // Notes on the sheet:
  //   ai + bi
  //   ai bi
endmodule
