// Logisim project pb6.circ as structural Verilog: 1 circuit, main circuit main
module main (
  input  a,
  input  b,
  input  a_2,
  input  a_3,
  input  b_2,
  output ab,
  output a_prime,
  output a_b
);

  wire nand_1_out, nand_3_out, nand_4_out;

  nand nand_1 (nand_1_out, a, b);
  nand nand_2 (a_prime, a_2, a_2);
  nand nand_3 (nand_3_out, a_3, a_3);
  nand nand_4 (nand_4_out, b_2, b_2);
  nand nand_5 (ab, nand_1_out, nand_1_out);
  nand nand_6 (a_b, nand_3_out, nand_4_out);

  // Notes on the sheet:
  //   AND
  //   NOT
  //   OR
endmodule
